# Fritzing sketch RGB_analog_Controller (saved by Fritzing 0.9.3b)
breadboards: 1

parts:
  Part1 = Arduino Mega 2560 (Rev3)
  Q1 = Basic FET N-Channel [package="TO220 [THT]"]
  Q2 = Basic FET N-Channel [package="TO220 [THT]"]
  Q3 = Basic FET N-Channel [package="TO220 [THT]"]
  RGB_Strip_LED1 = RGB Strip LED
  Power_plug1 = Power plug
  R1 = Rotary Potentiometer (Small) [maximum_resistance=100kΩ package=THT]
  R2 = Rotary Potentiometer (Small) [maximum_resistance=100kΩ package=THT]
  R3 = Rotary Potentiometer (Small) [maximum_resistance=100kΩ package=THT]

nets:
  N1: Part1.A0, R1.wiper
  N2: Part1.A1, R2.wiper
  N3: Part1.A2, R3.wiper
  GND: Part1.GND, Q1.source, Q2.source, Q3.source, Power_plug1.GND, R1.leg2, R2.leg2, R3.leg2
  N4: Part1.5V, R1.leg1, R2.leg1, R3.leg1
  N5: Part1.D2_PWM, Q3.gate
  N6: Part1.D3_PWM, Q2.gate
  N7: Part1.D4_PWM, Q1.gate
  N8: Q1.drain, RGB_Strip_LED1.Red_Connect
  N9: Q2.drain, RGB_Strip_LED1.Green_Connect
  N10: Q3.drain, RGB_Strip_LED1.Blue_Connect
  N11: RGB_Strip_LED1.Common_Connect, Power_plug1.VCC

custom parts:
  RGB Strip LED: A tri-color Strip LED with red, green and blue. Based on LED SMD 5050 RGB Pin order: common cathode - green - red - blue
